// Logisim project archiMinimale.circ as structural Verilog: 1 circuit, main circuit main
module main (
  input  in_1,
  input  in_2
);

  wire registerfile_1_p1, registerfile_1_p7;
  wire [4:0] rs, rt;
  wire [5:0] Co;
  wire [15:0] mipsprogramrom_1_p1;
  wire [31:0] adder_1_p1, adder_1_p3, Imm;

  // Adder adder_1: pin names not known; wires that end beside it: adder_1_p1, 32'h4, adder_1_p3, adder_1_p1
  Register #(.width(32), .trigger("falling")) register_1 (
    .D(adder_1_p3), .en(1'b1), .Q(adder_1_p1), .clk(in_1), .clr(in_2));
  // RegisterFile registerfile_1: pin names not known; wires that end beside it: registerfile_1_p1, in_1, 1'b1, rt, rs, in_2, registerfile_1_p7
  // MIPSProgramROM mipsprogramrom_1: pin names not known; wires that end beside it: {Co, rs, rt, mipsprogramrom_1_p1}
  // MIPS_ALU mips_alu_1: pin names not known; wires that end beside it: registerfile_1_p7, Imm, 4'b0011, registerfile_1_p1
  assign Imm = {{16{1'b0}}, mipsprogramrom_1_p1};  // Bit_Extender bit_extender_1

  // Other names for the same wires on the sheet: _0 = in_2; H = in_1
endmodule
